// Logisim project RISC 32.circ as structural Verilog
module main (
  input  CLR,
  output [5:0] disOpCode,
  output [4:0] disDestRC,
  output [4:0] disSrcRA,
  output [4:0] disRB,
  output [15:0] disImmVal
);

  wire CLK, clock_2_out, enRA, enRB, enRY, enRZ, enWrite, instrFetch, memLoad, memStore, or_1_out, or_2_out,
       selMUXB;
  wire [2:0] opALU;
  wire [4:0] AddressA, AddressB, AddressC;
  wire [15:0] adder_1_out, memAddress, multiplexer_3_out, PC;
  wire [31:0] alu_1_1_out, ImmVal, memData, memInData, multiplexer_1_out, multiplexer_2_out, RA_q, rf_1_p4,
       rf_1_p6, rf_1_p7;
  wire [31:16] RZ_q;

  // RF rf_1: pin names not known; wires that end beside it: AddressA, AddressB, CLK, rf_1_p4, CLR, rf_1_p6, rf_1_p7, AddressC, enWrite
  Register #(.width(32)) RA (.D(rf_1_p4), .en(enRA), .Q(RA_q), .clk(CLK), .clr(CLR));
  ALU_1 alu_1_1 (.InA(RA_q), .InB(multiplexer_2_out), .opALU(opALU), .Out(alu_1_1_out));
  Multiplexer #(.width(32)) multiplexer_1 (
    .in0({RZ_q, memAddress}), .in1(memData), .out(multiplexer_1_out), .sel(memLoad));  // open: en
  Register #(.width(32)) RB (.D(rf_1_p7), .en(enRB), .Q(memInData), .clk(CLK), .clr(CLR));
  Register #(.width(32)) RZ (.D(alu_1_1_out), .en(enRZ), .Q({RZ_q, memAddress}), .clk(CLK), .clr(CLR));
  Register #(.width(32)) RY (.D(multiplexer_1_out), .en(enRY), .Q(rf_1_p6), .clk(CLK), .clr(CLR));
  Multiplexer #(.width(32)) multiplexer_2 (
    .in0(memInData), .in1(ImmVal), .out(multiplexer_2_out), .sel(selMUXB));  // open: en
  Clock clock_1 (.out(CLK));
  or or_1 (or_1_out, memLoad, memStore);
  Register #(.width(32)) IR (
    .D(memData), .en(instrFetch), .Q({disOpCode, disDestRC, disSrcRA, disImmVal}), .clk(CLK), .clr(CLR));
  Multiplexer #(.width(16)) multiplexer_3 (
    .in0(PC), .in1(memAddress), .out(multiplexer_3_out), .sel(or_1_out));  // open: en
  CU cu_1 (
    .IR({disOpCode, disDestRC, disSrcRA, disImmVal}), .opALU(opALU), .AddressA(AddressA),
    .AddressB(AddressB), .AddressC(AddressC), .ImmVal(ImmVal), .Load(memLoad), .Store(memStore),
    .selMUXB(selMUXB), .CLK(CLK), .CLR(CLR), .enWrite(enWrite), .enRA(enRA), .enRB(enRB), .enRZ(enRZ),
    .enRY(enRY), .instFetch(instrFetch));
  Clock clock_2 (.out(clock_2_out));
  or or_2 (or_2_out, memLoad, instrFetch);
  RAM #(.addrWidth(16), .dataWidth(32), .bus("separate")) ram_1 (
    .addr(multiplexer_3_out), .din(memInData), .data(memData), .str(memStore), .clk(clock_2_out),
    .ld(or_2_out));  // open: sel, clr
  Adder #(.width(16)) adder_1 (.a(PC), .b(16'h1), .out(adder_1_out));  // open: cin, cout
  Register #(.width(16)) u_PC (.D(adder_1_out), .en(instrFetch), .Q(PC), .clk(CLK), .clr(CLR));

  assign disRB = disImmVal[4:0];
endmodule

module RF (
  input  EnWrite,
  input  [31:0] I1,
  input  CLK,
  input  CLR,
  input  [4:0] Address_A,
  input  [4:0] Address_C,
  input  [4:0] Address_B,
  output [31:0] O1,
  output [31:0] O2
);

  wire R1_W, R2_W, R3_W, R4_W, R5_W, R6_W, R7_W, R8_W, R9_W, R10_W, R11_W, R12_W, R13_W, R14_W, R15_W, R16_W,
       R17_W, R18_W, R19_W, R20_W, R21_W, R22_W, R23_W, R24_W, R25_W, R26_W, R27_W, R28_W, R29_W, R30_W,
       R31_W, R32_W;
  wire [31:0] R1_out, R2_out, R3_out, R4_out, R5_out, R6_out, R7_out, R8_out, R9_out, R10_out, R11_out,
       R12_out, R13_out, R14_out, R15_out, R16_out, R17_out, R18_out, R19_out, R20_out, R21_out, R22_out,
       R23_out, R24_out, R25_out, R26_out, R27_out, R28_out, R29_out, R30_out, R31_out, R32_out;

  Register #(.width(32)) register_1 (.D(I1), .en(R1_W), .Q(R1_out), .clk(CLK), .clr(CLR));
  Register #(.width(32)) register_2 (.D(I1), .en(R5_W), .Q(R5_out), .clk(CLK), .clr(CLR));
  Register #(.width(32)) register_3 (.D(I1), .en(R9_W), .Q(R9_out), .clk(CLK), .clr(CLR));
  Register #(.width(32)) register_4 (.D(I1), .en(R13_W), .Q(R13_out), .clk(CLK), .clr(CLR));
  Register #(.width(32)) register_5 (.D(I1), .en(R17_W), .Q(R17_out), .clk(CLK), .clr(CLR));
  Register #(.width(32)) register_6 (.D(I1), .en(R21_W), .Q(R21_out), .clk(CLK), .clr(CLR));
  Register #(.width(32)) register_7 (.D(I1), .en(R25_W), .Q(R25_out), .clk(CLK), .clr(CLR));
  Register #(.width(32)) register_8 (.D(I1), .en(R29_W), .Q(R29_out), .clk(CLK), .clr(CLR));
  Multiplexer #(.select(5), .width(32)) multiplexer_1 (
    .in0(R1_out), .in1(R2_out), .in2(R3_out), .in3(R4_out), .in4(R5_out), .in5(R6_out), .in6(R7_out),
    .in7(R8_out), .in8(R9_out), .in9(R10_out), .in10(R11_out), .in11(R12_out), .in12(R13_out),
    .in13(R14_out), .in14(R15_out), .in15(R16_out), .in16(R17_out), .in17(R18_out), .in18(R19_out),
    .in19(R20_out), .in20(R21_out), .in21(R22_out), .in22(R23_out), .in23(R24_out), .in24(R25_out),
    .in25(R26_out), .in26(R27_out), .in27(R28_out), .in28(R29_out), .in29(R30_out), .in30(R31_out),
    .in31(R32_out), .out(O1), .sel(Address_A));  // open: en
  Register #(.width(32)) register_9 (.D(I1), .en(R2_W), .Q(R2_out), .clk(CLK), .clr(CLR));
  Register #(.width(32)) register_10 (.D(I1), .en(R6_W), .Q(R6_out), .clk(CLK), .clr(CLR));
  Register #(.width(32)) register_11 (.D(I1), .en(R10_W), .Q(R10_out), .clk(CLK), .clr(CLR));
  Register #(.width(32)) register_12 (.D(I1), .en(R14_W), .Q(R14_out), .clk(CLK), .clr(CLR));
  Register #(.width(32)) register_13 (.D(I1), .en(R18_W), .Q(R18_out), .clk(CLK), .clr(CLR));
  Register #(.width(32)) register_14 (.D(I1), .en(R22_W), .Q(R22_out), .clk(CLK), .clr(CLR));
  Register #(.width(32)) register_15 (.D(I1), .en(R26_W), .Q(R26_out), .clk(CLK), .clr(CLR));
  Register #(.width(32)) register_16 (.D(I1), .en(R30_W), .Q(R30_out), .clk(CLK), .clr(CLR));
  Register #(.width(32)) register_17 (.D(I1), .en(R3_W), .Q(R3_out), .clk(CLK), .clr(CLR));
  Register #(.width(32)) register_18 (.D(I1), .en(R7_W), .Q(R7_out), .clk(CLK), .clr(CLR));
  Register #(.width(32)) register_19 (.D(I1), .en(R11_W), .Q(R11_out), .clk(CLK), .clr(CLR));
  Register #(.width(32)) register_20 (.D(I1), .en(R15_W), .Q(R15_out), .clk(CLK), .clr(CLR));
  Register #(.width(32)) register_21 (.D(I1), .en(R19_W), .Q(R19_out), .clk(CLK), .clr(CLR));
  Register #(.width(32)) register_22 (.D(I1), .en(R23_W), .Q(R23_out), .clk(CLK), .clr(CLR));
  Register #(.width(32)) register_23 (.D(I1), .en(R27_W), .Q(R27_out), .clk(CLK), .clr(CLR));
  Register #(.width(32)) register_24 (.D(I1), .en(R31_W), .Q(R31_out), .clk(CLK), .clr(CLR));
  Multiplexer #(.select(5), .width(32)) multiplexer_2 (
    .in0(R1_out), .in1(R2_out), .in2(R3_out), .in3(R4_out), .in4(R5_out), .in5(R6_out), .in6(R7_out),
    .in7(R8_out), .in8(R9_out), .in9(R10_out), .in10(R11_out), .in11(R12_out), .in12(R13_out),
    .in13(R14_out), .in14(R15_out), .in15(R16_out), .in16(R17_out), .in17(R18_out), .in18(R19_out),
    .in19(R20_out), .in20(R21_out), .in21(R22_out), .in22(R23_out), .in23(R24_out), .in24(R25_out),
    .in25(R26_out), .in26(R27_out), .in27(R28_out), .in28(R29_out), .in29(R30_out), .in30(R31_out),
    .in31(R32_out), .out(O2), .sel(Address_B));  // open: en
  Register #(.width(32)) register_25 (.D(I1), .en(R4_W), .Q(R4_out), .clk(CLK), .clr(CLR));
  Register #(.width(32)) register_26 (.D(I1), .en(R8_W), .Q(R8_out), .clk(CLK), .clr(CLR));
  Register #(.width(32)) register_27 (.D(I1), .en(R12_W), .Q(R12_out), .clk(CLK), .clr(CLR));
  Register #(.width(32)) register_28 (.D(I1), .en(R16_W), .Q(R16_out), .clk(CLK), .clr(CLR));
  Register #(.width(32)) register_29 (.D(I1), .en(R20_W), .Q(R20_out), .clk(CLK), .clr(CLR));
  Register #(.width(32)) register_30 (.D(I1), .en(R24_W), .Q(R24_out), .clk(CLK), .clr(CLR));
  Register #(.width(32)) register_31 (.D(I1), .en(R28_W), .Q(R28_out), .clk(CLK), .clr(CLR));
  Register #(.width(32)) register_32 (.D(I1), .en(R32_W), .Q(R32_out), .clk(CLK), .clr(CLR));
  Demultiplexer #(.select(5), .enable("false")) demultiplexer_1 (
    .out0(R1_W), .out1(R2_W), .out2(R3_W), .out3(R4_W), .out4(R5_W), .out5(R6_W), .out6(R7_W), .out7(R8_W),
    .out8(R9_W), .out9(R10_W), .out10(R11_W), .out11(R12_W), .out12(R13_W), .out13(R14_W), .out14(R15_W),
    .out15(R16_W), .out16(R17_W), .out17(R18_W), .out18(R19_W), .out19(R20_W), .out20(R21_W), .out21(R22_W),
    .out22(R23_W), .out23(R24_W), .out24(R25_W), .out25(R26_W), .out26(R27_W), .out27(R28_W), .out28(R29_W),
    .out29(R30_W), .out30(R31_W), .out31(R32_W), .in(EnWrite), .sel(Address_C));

  // Other names for the same wires on the sheet: R_in[31:0] = I1
endmodule

module ALU_1 (
  input  [31:0] InA,
  input  [31:0] InB,
  input  [2:0] opALU,
  output [31:0] Out
);

  wire [31:0] adder_1_out, and_1_out, or_1_out, subtractor_1_out;

  Adder #(.width(32)) adder_1 (.a(InA), .b(InB), .out(adder_1_out));  // open: cin, cout
  Subtractor #(.width(32)) subtractor_1 (.a(InA), .b(InB), .out(subtractor_1_out));  // open: bin, bout
  assign and_1_out = InA & InB;  // AND_Gate and_1, 32 bits wide
  assign or_1_out = InA | InB;  // OR_Gate or_1, 32 bits wide
  Multiplexer #(.select(3), .width(32)) multiplexer_1 (
    .in0(adder_1_out), .in1(subtractor_1_out), .in2(and_1_out), .in3(or_1_out), .in4(InB), .in5(InB),
    .in6(InB), .in7(InB), .out(Out), .sel(opALU));  // open: en
endmodule

module CU (
  input  [31:0] IR,
  input  CLK,
  input  CLR,
  output [2:0] opALU,
  output [4:0] AddressA,
  output [4:0] AddressB,
  output [4:0] AddressC,
  output [31:0] ImmVal,
  output instFetch,
  output Load,
  output Store,
  output selMUXB,
  output enRA,
  output enRB,
  output enRZ,
  output enRY,
  output enWrite
);

  wire initSys, instrADD, instrAND, instrLoad, instrMov, instrMovIm, instrOR, instrStore, instrSUB, noOp,
       not_1_out, opAdd, or_3_out, shift_register_1_out, Stage5;

  Decoder #(.select(3)) decoder_1 (
    .out0(instrMov), .out1(instrMovIm), .out2(instrLoad), .out3(instrStore), .out4(instrADD),
    .out5(instrSUB), .out6(instrAND), .out7(instrOR), .sel(IR[31:29]));  // open: en
  or or_1 (opAdd, instrADD, instrLoad, instrStore);
  or or_2 (noOp, instrMov, instrMovIm);
  Priority_Encoder priority_encoder_1 (
    .in0(opAdd), .in1(instrSUB), .in2(instrAND), .in3(instrOR), .in7(noOp), .out(opALU));  // open: in4, in5, in6, en_in, gs, en_out
  or or_3 (or_3_out, shift_register_1_out, initSys);
  Shift_Register #(.length(5)) shift_register_1 (
    .in(or_3_out), .clk(CLK), .out(shift_register_1_out), .clr(CLR), .q0(instFetch), .q1(enRA), .q2(enRZ),
    .q3(enRY), .q4(Stage5));  // open: shift, load, d0, d1, d2, d3, d4
  Multiplexer #(.width(5)) multiplexer_1 (
    .in0(IR[4:0]), .in1(IR[25:21]), .out(AddressB), .sel(instrStore));  // open: en
  not not_1 (not_1_out, Store);
  and and_1 (enWrite, not_1_out, Stage5);
  and and_2 (Load, enRY, instrLoad);
  and and_3 (Store, enRY, instrStore);
  nor nor_1 (initSys, instFetch, enRA, enRZ, enRY, Stage5);

  assign AddressA = IR[20:16];
  assign AddressC = IR[25:21];
  assign enRB = enRA;
  assign ImmVal = {{16{1'b0}}, IR[15:0]};
  assign selMUXB = IR[28];

  // Other names for the same wires on the sheet: ImmVal16[15:0] = IR[15:0]; instrSrcRB[4:0] = IR[4:0];
  //   srcRA[4:0] = IR[20:16]; destRC[4:0] = IR[25:21]; opCode[5:0] = IR[31:26]; srcRB[4:0] = AddressB;
  //   Stage1 = instFetch; Stage2 = enRA; Stage3 = enRZ; Stage4 = enRY

  // Notes on the sheet:
  //   Instruction Decoding
  //   Src and ImmVal
  //   Clocking Mech.
endmodule
